# Fritzing sketch Project (saved by Fritzing 0.9.3b)
breadboards: 1

parts:
  Raspberry_Pi_1 = Raspberry Pi 3 [part_number=RPI-3-V1.2]
  U1 = LCD-16X2 [package=lcd-8x2-kit]
  R1 = Trimmer Potentiometer [maximum_resistance=10kΩ package=THT]
  ADC1 = MCP3008 [package=dil16]
  J1 = Piezo Speaker
  R2 = Trimmer Potentiometer [maximum_resistance=10kΩ package=THT]
  R3 = Resistor [tolerance=±5% resistance=10k package=THT]
  R4 = Photocell (LDR) [package=THT]
  DS1 = DS18B20 1-Wire Temperature Sensor [part_number=DS18B20]

nets:
  3V3: Raspberry_Pi_1.3v3, Raspberry_Pi_1.3V3, ADC1.VREF, ADC1.VDD, R2.leg2, R3.Pin_1
  N1: Raspberry_Pi_1.GPIO4, DS1.DQ
  N2: Raspberry_Pi_1.GPIO10, ADC1.Din
  N3: Raspberry_Pi_1.GPIO9, ADC1.Dout
  N4: Raspberry_Pi_1.GPIO11, ADC1.CLK
  N5: Raspberry_Pi_1.GPIO6, J1.pin1
  N6: Raspberry_Pi_1.GPIO13, U1.DB7
  N7: Raspberry_Pi_1.GPIO19, U1.DB6
  N8: Raspberry_Pi_1.GPIO26, U1.DB5
  GND: Raspberry_Pi_1.GND, U1.VSS, U1.R_W, U1.K, R1.leg2, ADC1.DGND, ADC1.AGND, J1.pin2, R2.leg1, R4.pin_0, DS1.GND
  N9: Raspberry_Pi_1.GPIO21, U1.RS
  N10: Raspberry_Pi_1.GPIO20, U1.E
  N11: Raspberry_Pi_1.GPIO16, U1.DB0
  N12: Raspberry_Pi_1.GPIO12, U1.DB1
  N13: Raspberry_Pi_1.GPIO8, ADC1.CS/SHDN
  N14: Raspberry_Pi_1.GPIO25, U1.DB2
  N15: Raspberry_Pi_1.GPIO24, U1.DB3
  N16: Raspberry_Pi_1.GPIO23, U1.DB4
  VDD: Raspberry_Pi_1.5V, U1.VDD, U1.A, R1.leg1, DS1.VDD
  N17: U1.VO, R1.wiper
  N18: ADC1.CH0, R2.wiper
  N19: ADC1.CH1, R3.Pin_0, R4.pin_1
