# Fritzing sketch ProjectBreadboard (saved by Fritzing 0.9.3b)
breadboards: 1

parts:
  ADC1 = MCP3008 [package=dil16]
  R1 = Trimmer Potentiometer [maximum_resistance=10kΩ package=THT]
  R2 = Trimmer Potentiometer [maximum_resistance=10kΩ package=THT]
  J1 = Piezo Speaker
  R4 = Photocell (LDR) [package=THT]
  Raspberry_Pi_1 = Raspberry Pi 3 [part_number=RPI-3-V1.2]
  DS1 = DS18B20 1-Wire Temperature Sensor [part_number=DS18B20]
  R3 = Resistor [tolerance=±5% resistance=10k package=THT]
  U1 = LCD-16X2 [package=lcd-16x2_noholes]

nets (from the schematic view):
  N1: ADC1.CH0, R2.wiper
  N2: ADC1.CH1, R4.pin_1, R3.Pin_0
  GND: ADC1.DGND, ADC1.AGND, R1.leg2, R2.leg1, J1.pin2, R4.pin_0, Raspberry_Pi_1.GND, DS1.GND, U1.VSS, U1.R_W, U1.K
  N3: ADC1.CS/SHDN, Raspberry_Pi_1.GPIO8
  N4: ADC1.Din, Raspberry_Pi_1.GPIO10
  N5: ADC1.Dout, Raspberry_Pi_1.GPIO9
  N6: ADC1.CLK, Raspberry_Pi_1.GPIO11
  3V3: ADC1.VREF, ADC1.VDD, R2.leg2, Raspberry_Pi_1.3v3, Raspberry_Pi_1.3V3, R3.Pin_1
  VDD: R1.leg1, Raspberry_Pi_1.5V, DS1.VDD, U1.VDD, U1.A
  N7: R1.wiper, U1.VO
  N8: J1.pin1, Raspberry_Pi_1.GPIO6
  N9: Raspberry_Pi_1.GPIO4, DS1.DQ
  N10: Raspberry_Pi_1.GPIO13, U1.DB7
  N11: Raspberry_Pi_1.GPIO19, U1.DB6
  N12: Raspberry_Pi_1.GPIO26, U1.DB5
  N13: Raspberry_Pi_1.GPIO21, U1.RS
  N14: Raspberry_Pi_1.GPIO20, U1.E
  N15: Raspberry_Pi_1.GPIO16, U1.DB0
  N16: Raspberry_Pi_1.GPIO12, U1.DB1
  N17: Raspberry_Pi_1.GPIO25, U1.DB2
  N18: Raspberry_Pi_1.GPIO24, U1.DB3
  N19: Raspberry_Pi_1.GPIO23, U1.DB4
